# Fritzing sketch PresenDuino (saved by Fritzing 0.8.7b)
breadboards: 1

parts:
  Part1 = Arduino Uno (Rev3)  # not connected
  U1 = XBee
  LCD1 = LCD screen  # not connected
  S1 = Pushbutton [package="[THT]"]
  S2 = Pushbutton [package="[THT]"]
  R1 = Resistor [tolerance=±5% resistance=1k package=THT]
  R1_2 = Resistor [tolerance=±5% resistance=1k package=THT]
  R2 = Rotary Potentiometer (Small) [maximum_resistance=100kΩ package=THT]  # not connected

nets:
  N1: U1.pin3, U1.pin18
  N2: U1.pin4, U1.pin17
  N3: S1.Pin_1, S1.Pin_2
  N4: S1.Pin_3, S1.Pin_4, R1_2.Pin_1
  N5: S2.Pin_1, S2.Pin_2
  N6: S2.Pin_3, S2.Pin_4, R1.Pin_1
